# Fritzing sketch OLED_ssd1306 (saved by Fritzing 0.9.10b)
breadboards: 1

parts:
  V1 = DC Power [voltage=5]
  Mod1 = Amica NodeMCU DEVKIT 1.0
  OLED_I2C1 = OLED 128x64 I2C Monochrome Display

nets:
  N1: V1.V-, Mod1.pin2, Mod1.pin_9, OLED_I2C1.GND
  N2: Mod1.pin1, Mod1.pin_10, OLED_I2C1.VDD
  N3: Mod1.pin_13, OLED_I2C1.SDA
  N4: Mod1.pin_14, OLED_I2C1.SCK
